// Digital circuit 12-Mux4Way16.dig as structural Verilog
module _12_Mux4Way16 (
  input  [15:0] a,
  input  [15:0] b,
  input  [15:0] c,
  input  [15:0] d,
  input  [1:0] sel,
  output [15:0] out
);

  wire [15:0] multiplexer_1_out, multiplexer_2_out;

  Multiplexer #(.Bits(16)) multiplexer_1 (.sel(sel[0]), .in_0(a), .in_1(b), .out(multiplexer_1_out));
  Multiplexer #(.Bits(16)) multiplexer_2 (.sel(sel[0]), .in_0(c), .in_1(d), .out(multiplexer_2_out));
  Multiplexer #(.Bits(16)) multiplexer_3 (.sel(sel[1]), .in_0(multiplexer_1_out), .in_1(multiplexer_2_out), .out(out));

  // Notes on the sheet:
  //   12 - Mux4Way16
endmodule
