// Digital circuit 13 - Mux8Way16.dig as structural Verilog
module _13___Mux8Way16 (
  input  [15:0] a,
  input  [15:0] b,
  input  [15:0] c,
  input  [15:0] d,
  input  [15:0] e,
  input  [15:0] f,
  input  [15:0] g,
  input  [15:0] h,
  input  [2:0] sel,
  output [15:0] out
);

  wire [15:0] multiplexer_1_out, multiplexer_2_out;

  Multiplexer #(.Bits(16), .Selector_Bits(2)) multiplexer_1 (
    .sel(sel[1:0]), .in_0(a), .in_1(b), .in_2(c), .in_3(d), .out(multiplexer_1_out));
  Multiplexer #(.Selector_Bits(2), .Bits(16)) multiplexer_2 (
    .sel(sel[1:0]), .in_0(e), .in_1(f), .in_2(g), .in_3(h), .out(multiplexer_2_out));
  Multiplexer #(.Bits(16)) multiplexer_3 (.sel(sel[2]), .in_0(multiplexer_1_out), .in_1(multiplexer_2_out), .out(out));

  // Notes on the sheet:
  //   13 - Mux8Way16
endmodule
