// Digital circuit And16.dig as structural Verilog
module And16 (
  input  [15:0] b,
  input  [15:0] a,
  output [15:0] out
);

  and and_1 (out[0], a[0], b[0]);
  and and_2 (out[1], a[1], b[1]);
  and and_3 (out[2], a[2], b[2]);
  and and_4 (out[3], a[3], b[3]);
  and and_5 (out[4], a[4], b[4]);
  and and_6 (out[5], a[5], b[5]);
  and and_7 (out[6], a[6], b[6]);
  and and_8 (out[7], a[7], b[7]);
  and and_9 (out[8], a[8], b[8]);
  and and_10 (out[9], a[9], b[9]);
  and and_11 (out[10], a[10], b[10]);
  and and_12 (out[11], a[11], b[11]);
  and and_13 (out[12], a[12], b[12]);
  and and_14 (out[13], a[13], b[13]);
  and and_15 (out[14], a[14], b[14]);
  and and_16 (out[15], a[15], b[15]);

  // Notes on the sheet:
  //   8 - And16
endmodule
