// Digital circuit Mux16.dig as structural Verilog
module Mux16 (
  input  [15:0] b,
  input  [15:0] a,
  input  sel,
  output [15:0] out
);

  Multiplexer multiplexer_1 (.sel(sel), .in_0(a[0]), .in_1(b[0]), .out(out[0]));
  Multiplexer multiplexer_2 (.sel(sel), .in_0(a[1]), .in_1(b[1]), .out(out[1]));
  Multiplexer multiplexer_3 (.sel(sel), .in_0(a[2]), .in_1(b[2]), .out(out[2]));
  Multiplexer multiplexer_4 (.sel(sel), .in_0(a[3]), .in_1(b[3]), .out(out[3]));
  Multiplexer multiplexer_5 (.sel(sel), .in_0(a[4]), .in_1(b[4]), .out(out[4]));
  Multiplexer multiplexer_6 (.sel(sel), .in_0(a[5]), .in_1(b[5]), .out(out[5]));
  Multiplexer multiplexer_7 (.sel(sel), .in_0(a[6]), .in_1(b[6]), .out(out[6]));
  Multiplexer multiplexer_8 (.sel(sel), .in_0(a[7]), .in_1(b[7]), .out(out[7]));
  Multiplexer multiplexer_9 (.sel(sel), .in_0(a[8]), .in_1(b[8]), .out(out[8]));
  Multiplexer multiplexer_10 (.sel(sel), .in_0(a[9]), .in_1(b[9]), .out(out[9]));
  Multiplexer multiplexer_11 (.sel(sel), .in_0(a[10]), .in_1(b[10]), .out(out[10]));
  Multiplexer multiplexer_12 (.sel(sel), .in_0(a[11]), .in_1(b[11]), .out(out[11]));
  Multiplexer multiplexer_13 (.sel(sel), .in_0(a[12]), .in_1(b[12]), .out(out[12]));
  Multiplexer multiplexer_14 (.sel(sel), .in_0(a[13]), .in_1(b[13]), .out(out[13]));
  Multiplexer multiplexer_15 (.sel(sel), .in_0(a[14]), .in_1(b[14]), .out(out[14]));
  Multiplexer multiplexer_16 (.sel(sel), .in_0(a[15]), .in_1(b[15]), .out(out[15]));

  // Notes on the sheet:
  //   10 - Mux16
endmodule
