// Digital circuit Not16.dig as structural Verilog
module Not16 (
  input  [15:0] in,
  output [15:0] out
);

  not not_1 (out[0], in[0]);
  not not_2 (out[1], in[1]);
  not not_3 (out[2], in[2]);
  not not_4 (out[3], in[3]);
  not not_5 (out[4], in[4]);
  not not_6 (out[5], in[5]);
  not not_7 (out[6], in[6]);
  not not_8 (out[7], in[7]);
  not not_9 (out[8], in[8]);
  not not_10 (out[9], in[9]);
  not not_11 (out[10], in[10]);
  not not_12 (out[11], in[11]);
  not not_13 (out[12], in[12]);
  not not_14 (out[13], in[13]);
  not not_15 (out[14], in[14]);
  not not_16 (out[15], in[15]);

  // Notes on the sheet:
  //   7 - Not16
endmodule
