// Digital circuit Or16.dig as structural Verilog
module Or16 (
  input  [15:0] b,
  input  [15:0] a,
  output [15:0] out
);

  or or_1 (out[0], a[0], b[0]);
  or or_2 (out[1], a[1], b[1]);
  or or_3 (out[2], a[2], b[2]);
  or or_4 (out[3], a[3], b[3]);
  or or_5 (out[4], a[4], b[4]);
  or or_6 (out[5], a[5], b[5]);
  or or_7 (out[6], a[6], b[6]);
  or or_8 (out[7], a[7], b[7]);
  or or_9 (out[8], a[8], b[8]);
  or or_10 (out[9], a[9], b[9]);
  or or_11 (out[10], a[10], b[10]);
  or or_12 (out[11], a[11], b[11]);
  or or_13 (out[12], a[12], b[12]);
  or or_14 (out[13], a[13], b[13]);
  or or_15 (out[14], a[14], b[14]);
  or or_16 (out[15], a[15], b[15]);

  // Notes on the sheet:
  //   9 - Or16
endmodule
