// Digital circuit Or8Way.dig as structural Verilog
module Or8Way (
  input  [7:0] in,
  output out_2
);

  wire or_1_out, or_2_out, or_3_out, or_4_out, or_5_out, or_6_out;

  or or_1 (or_1_out, in[0], in[1]);
  or or_2 (or_2_out, or_1_out, in[2]);
  or or_3 (or_3_out, or_2_out, in[3]);
  or or_4 (or_4_out, or_3_out, in[4]);
  or or_5 (or_5_out, or_4_out, in[5]);
  or or_6 (or_6_out, or_5_out, in[6]);
  or or_7 (out_2, or_6_out, in[7]);

  // Notes on the sheet:
  //   11 - Or8Way
endmodule
