// Digital circuit mux_dmux.dig as structural Verilog
module mux_dmux (
  input  a,
  input  b,
  input  sel,
  input  in,
  input  sel_2,
  output out,
  output a_2,
  output b_2
);

  wire and_1_out, and_2_out, not_1_out, not_2_out;

  not not_1 (not_1_out, sel);
  not not_2 (not_2_out, sel_2);
  and and_1 (and_1_out, a, not_1_out);
  and and_2 (and_2_out, b, sel);
  and and_3 (a_2, in, not_2_out);
  and and_4 (b_2, in, sel_2);
  or or_1 (out, and_1_out, and_2_out);

  // Notes on the sheet:
  //   5 - Mux
  //   6 - DMux
endmodule
