// Digital circuit PCcounterJumpLogic.dig as structural Verilog
module PCcounterJumpLogic (
  input  j1___LT,
  input  zr,
  input  ng,
  input  j2___EQ,
  input  j3___GT,
  output load
);

  wire GrtTn, gt, LessTn, multiplexer_1_out, multiplexer_2_out, multiplexer_3_out, multiplexer_4_out,
       multiplexer_5_out, multiplexer_6_out, not_1_out, not_2_out, zero;

  and and_1 (GrtTn, j3___GT, gt);
  and and_2 (zero, j2___EQ, zr);
  and and_3 (LessTn, ng, j1___LT);
  not not_1 (not_1_out, zr);
  not not_2 (not_2_out, ng);
  and and_4 (gt, not_1_out, not_2_out);
  Multiplexer multiplexer_1 (.sel(GrtTn), .in_0(1'b0), .in_1(1'b1), .out(multiplexer_1_out));
  Multiplexer multiplexer_2 (.sel(GrtTn), .in_0(1'b1), .in_1(1'b1), .out(multiplexer_2_out));
  Multiplexer multiplexer_3 (.sel(GrtTn), .in_0(1'b1), .in_1(1'b1), .out(multiplexer_3_out));
  Multiplexer multiplexer_4 (.sel(GrtTn), .in_0(1'b1), .in_1(1'b1), .out(multiplexer_4_out));
  Multiplexer multiplexer_5 (.sel(zero), .in_0(multiplexer_1_out), .in_1(multiplexer_2_out), .out(multiplexer_5_out));
  Multiplexer multiplexer_6 (.sel(zero), .in_0(multiplexer_3_out), .in_1(multiplexer_4_out), .out(multiplexer_6_out));
  Multiplexer multiplexer_7 (.sel(LessTn), .in_0(multiplexer_5_out), .in_1(multiplexer_6_out), .out(load));
endmodule
